# Fritzing sketch Wiring_fritzing (saved by Fritzing 0.9.4)

parts:
  Raspberry_Pi_4_Mod_B = Raspberry Pi 4B  # not connected
  Q1 = Basic FET P-Channel [package="TO220 [THT]"]  # not connected
  D2 = Rectifier Diode [part_number=1N4001 package="Melf DO-213 AB [SMD]"]
  D1 = Rectifier Diode [part_number=1N4001 package="Melf DO-213 AB [SMD]"]
  Buck_DC/DC = RioRand LM2596
  L1_2_2mH = Inductor [package="400 mil [THT]"]  # not connected
  U1 = LIPO-2000mAh [package=lipo-2000]  # not connected
  R1 = Resistor [tolerance=±5% resistance=220 package="0603 [SMD]"]  # not connected

nets:
  N1: D2.cathode, D1.cathode, Buck_DC/DC.Pin_1
